// Logisim project fulladder.circ as structural Verilog: 4 circuits, main circuit main
module main (
  input  C,
  input  A,
  input  B,
  output Sum,
  output Carry
);

  wire halfadder_1_carry, halfadder_1_sum, halfadder_2_p4;

  halfadder halfadder_1 (.a(A), .b(B), .sum(halfadder_1_sum), .carry(halfadder_1_carry));
  // halfadder halfadder_2: pin names not known; wires that end beside it: halfadder_1_sum, C, Sum, halfadder_2_p4
  or or_1 (Carry, halfadder_2_p4, halfadder_1_carry);
endmodule

module halfadder (
  input  a,
  input  b,
  output sum,
  output carry
);

  xor xor_1 (sum, a, b);
  and and_1 (carry, a, b);
endmodule

module fulladder (
  input  carryin,
  input  a,
  input  b,
  output Sum,
  output Carryout
);

  wire and_1_out, and_2_out, xor_1_out;

  xor xor_1 (xor_1_out, a, b);
  and and_1 (and_1_out, a, b);
  xor xor_2 (Sum, carryin, xor_1_out);
  and and_2 (and_2_out, carryin, xor_1_out);
  or or_1 (Carryout, and_2_out, and_1_out);
endmodule

module eightbits (
  input  in_1,
  input  in_2,
  input  in_3,
  input  in_4,
  input  in_5,
  input  in_6,
  input  in_7,
  input  in_8,
  input  in_9,
  input  in_10,
  input  in_11,
  input  in_12,
  input  in_13,
  input  in_14,
  input  in_15,
  input  in_16,
  output out_17,
  output out_18,
  output out_19,
  output out_20,
  output out_21,
  output out_22,
  output out_23,
  output out_24,
  output out_25
);

  wire fulladder_1_carryout, fulladder_3_carryout, fulladder_5_carryout, fulladder_7_carryout,
       fulladder_9_carryout, fulladder_11_p3, halfadder_1_carry, undriven, undriven_2, undriven_3,
       undriven_4, undriven_5, undriven_6, undriven_7, undriven_8, undriven_9, undriven_10;

  halfadder halfadder_1 (.a(in_1), .b(in_2), .sum(out_17), .carry(halfadder_1_carry));
  fulladder fulladder_1 (
    .carryin(halfadder_1_carry), .a(in_3), .b(in_4), .Sum(out_18), .Carryout(fulladder_1_carryout));
  fulladder fulladder_2 (
    .carryin(halfadder_1_carry), .a(in_3), .b(in_4), .Sum(out_18), .Carryout(fulladder_1_carryout));
  fulladder fulladder_3 (
    .carryin(fulladder_1_carryout), .a(undriven), .b(undriven_2), .Sum(out_19),
    .Carryout(fulladder_3_carryout));
  fulladder fulladder_4 (
    .carryin(fulladder_1_carryout), .a(undriven), .b(undriven_2), .Sum(out_19),
    .Carryout(fulladder_3_carryout));
  fulladder fulladder_5 (
    .carryin(fulladder_3_carryout), .a(undriven_3), .b(undriven_4), .Sum(out_20),
    .Carryout(fulladder_5_carryout));
  fulladder fulladder_6 (
    .carryin(fulladder_3_carryout), .a(undriven_3), .b(undriven_4), .Sum(out_20),
    .Carryout(fulladder_5_carryout));
  fulladder fulladder_7 (
    .carryin(fulladder_5_carryout), .a(undriven_5), .b(undriven_6), .Sum(out_21),
    .Carryout(fulladder_7_carryout));
  fulladder fulladder_8 (
    .carryin(fulladder_5_carryout), .a(undriven_5), .b(undriven_6), .Sum(out_21),
    .Carryout(fulladder_7_carryout));
  fulladder fulladder_9 (
    .carryin(fulladder_7_carryout), .a(undriven_7), .b(undriven_8), .Sum(out_22),
    .Carryout(fulladder_9_carryout));
  fulladder fulladder_10 (
    .carryin(fulladder_7_carryout), .a(undriven_7), .b(undriven_8), .Sum(out_22),
    .Carryout(fulladder_9_carryout));
  // fulladder fulladder_11: pin names not known; wires that end beside it: out_23, fulladder_9_carryout, fulladder_11_p3, in_13, in_14
  fulladder fulladder_12 (.carryin(fulladder_11_p3), .a(undriven_9), .b(undriven_10), .Sum(out_24), .Carryout(out_25));
  fulladder fulladder_13 (.carryin(fulladder_11_p3), .a(undriven_9), .b(undriven_10), .Sum(out_24), .Carryout(out_25));
endmodule
